// Logisim project LogiTest.circ as structural Verilog: 1 circuit, main circuit main
module main (
  input  in_1,
  input  in_2,
  input  B,
  input  C,
  input  D,
  output out_6
);

  wire and_1_out, and_2_out, and_3_out, not_1_out, not_2_out, not_3_out, not_4_out, not_5_out, or_2_out;

  not not_1 (not_1_out, D);
  not not_2 (not_2_out, in_1);
  not not_3 (not_3_out, B);
  not not_4 (not_4_out, C);
  and and_1 (and_1_out, not_2_out, B);
  and and_2 (and_2_out, in_1, B, C);
  not not_5 (not_5_out, in_1);
  and and_3 (and_3_out, not_5_out, not_3_out, not_4_out, not_1_out);
  or or_1 (out_6, and_1_out, and_2_out, and_3_out);
  or or_2 (or_2_out, and_1_out, out_6);

  // Notes on the sheet:
  //   A
  //   /A.B + A.B.C + /A./B./C./D
endmodule
