// Logisim project Week3Prac.circ as structural Verilog: 1 circuit, main circuit main
module main (
  input  A,
  input  B,
  input  C___IN,
  input  A_2,
  input  B_2,
  input  C___IN_2,
  input  A_3,
  input  B_3,
  input  C___IN_3,
  input  A_4,
  input  B_4,
  input  C___IN_4,
  output out_13,
  output out_14,
  output out_15,
  output out_16,
  output out_17,
  output out_18,
  output out_19,
  output out_20
);

  wire and_1_out, and_2_out, and_3_out, and_4_out, and_5_out, and_6_out, and_7_out, and_8_out, xor_1_out,
       xor_2_out, xor_3_out, xor_4_out;

  xor xor_1 (xor_1_out, A, B);
  xor xor_2 (xor_2_out, A_2, B_2);
  xor xor_3 (xor_3_out, A_3, B_3);
  xor xor_4 (xor_4_out, A_4, B_4);
  and and_1 (and_1_out, xor_1_out, C___IN);
  and and_2 (and_2_out, B, A);
  and and_3 (and_3_out, xor_2_out, C___IN_2);
  and and_4 (and_4_out, B_2, A_2);
  and and_5 (and_5_out, xor_3_out, C___IN_3);
  and and_6 (and_6_out, B_3, A_3);
  and and_7 (and_7_out, xor_4_out, C___IN_4);
  and and_8 (and_8_out, B_4, A_4);
  xor xor_5 (out_13, xor_1_out, C___IN);
  or or_1 (out_14, and_1_out, and_2_out);
  xor xor_6 (out_15, xor_2_out, C___IN_2);
  or or_2 (out_16, and_3_out, and_4_out);
  xor xor_7 (out_17, xor_3_out, C___IN_3);
  or or_3 (out_18, and_5_out, and_6_out);
  xor xor_8 (out_19, xor_4_out, C___IN_4);
  or or_4 (out_20, and_7_out, and_8_out);
endmodule
